// Logisim project test.circ as structural Verilog: 2 circuits, main circuit main
module main (
);

  mux mux_1 ();  // open: A, Out
endmodule

// MUX
module mux (
  input  A,
  output Out
);


  assign Out = A;
endmodule
